# Fritzing sketch sketch (saved by Fritzing 0.9.3b)
breadboards: 1

parts:
  Raspberry_Pi_1 = Raspberry Pi 3 [part_number=RPI-3-V1.2]
  Part1 = SRF05 Ultrasonic Rangefinder
  R1 = Resistor [tolerance=±5% resistance=330 package=THT]
  R2 = Resistor [tolerance=±5% resistance=470 package=THT]
  LED1 = RGB LED (com. cathode, rgb) [package="5 mm [THT]"]
  R3 = Resistor [tolerance=±5% resistance=220 package=THT]
  R4 = Resistor [tolerance=±5% resistance=220 package=THT]
  R5 = Resistor [tolerance=±5% resistance=220 package=THT]

nets:
  N1: Raspberry_Pi_1.GPIO3, Part1.GND, R2.Pin_0
  N2: Raspberry_Pi_1.GIPO5, Part1.Trig
  N3: Raspberry_Pi_1.GIPO6, Raspberry_Pi_1.GIPO19, Raspberry_Pi_1.GIPO26, R3.Pin_0, R4.Pin_0, R5.Pin_0
  N4: Raspberry_Pi_1.GIPO13, R1.Pin_1, R2.Pin_1
  N5: Raspberry_Pi_1.GND, LED1.common_cathode
  5V: Raspberry_Pi_1.5V, Part1.VCC
  N6: Part1.Echo, R1.Pin_0
  N7: LED1.red_anode, R3.Pin_1
  N8: LED1.green_anode, R4.Pin_1
  N9: LED1.blue_anode, R5.Pin_1
